// Logisim project Binary to BCD using MUX.circ as structural Verilog: 1 circuit, main circuit main
module main (
  input  D,
  input  _0,
  input  _1,
  input  [2:0] in_4,
  output D0,
  output D1,
  output D2,
  output D3,
  output D4
);

  Multiplexer #(.select(3), .enable("false")) multiplexer_1 (
    .in0(D), .in1(D), .in2(D), .in3(D), .in4(D), .in5(D), .in6(D), .in7(D), .out(D0), .sel(in_4));
  Multiplexer #(.select(3), .enable("false")) multiplexer_2 (
    .in0(_0), .in1(_1), .in2(_0), .in3(_1), .in4(_0), .in5(_0), .in6(_1), .in7(_0), .out(D1), .sel(in_4));
  Multiplexer #(.select(3), .enable("false")) multiplexer_3 (
    .in0(_0), .in1(_0), .in2(_1), .in3(_1), .in4(_0), .in5(_0), .in6(_0), .in7(_1), .out(D2), .sel(in_4));
  Multiplexer #(.select(3), .enable("false")) multiplexer_4 (
    .in0(_0), .in1(_0), .in2(_0), .in3(_0), .in4(_1), .in5(_0), .in6(_0), .in7(_0), .out(D3), .sel(in_4));
  Multiplexer #(.select(3), .enable("false")) multiplexer_5 (
    .in0(_0), .in1(_0), .in2(_0), .in3(_0), .in4(_0), .in5(_1), .in6(_1), .in7(_1), .out(D4), .sel(in_4));
endmodule
