// Logisim project 4 to 16 decoder by 3 to 8 with enable.circ as structural Verilog: 1 circuit, main circuit main
module main (
  input  E,
  input  A,
  input  B,
  input  C,
  output Y5,
  output Y13
);

  wire not_1_out, not_2_out, not_3_out, not_4_out;

  not not_1 (not_1_out, E);
  not not_2 (not_2_out, A);
  not not_3 (not_3_out, B);
  not not_4 (not_4_out, C);
  and and_1 (Y5, not_1_out, A, not_3_out, C);
  and and_2 (Y13, E, A, not_3_out, C);
endmodule
