// Logisim project 8 to 1 mux by 4 to 1 and 2 to 1 with enable.circ as structural Verilog: 1 circuit, main circuit main
module main (
  input  D0,
  input  D1,
  input  D2,
  input  D3,
  input  [1:0] in_5,
  input  D4,
  input  D5,
  input  in_8,
  input  D6,
  input  D7,
  input  S2__MSB,
  output Y
);

  wire multiplexer_1_out, multiplexer_2_out, not_1_out;

  not not_1 (not_1_out, S2__MSB);
  Multiplexer #(.select(2)) multiplexer_1 (
    .in0(D0), .in1(D1), .in2(D2), .in3(D3), .out(multiplexer_1_out), .sel(in_5), .en(not_1_out));
  Multiplexer #(.select(2)) multiplexer_2 (
    .in0(D4), .in1(D5), .in2(D6), .in3(D7), .out(multiplexer_2_out), .sel(in_5), .en(S2__MSB));
  Multiplexer multiplexer_3 (.in0(multiplexer_1_out), .in1(multiplexer_2_out), .out(Y), .sel(S2__MSB), .en(in_8));
endmodule
