// Logisim project Addar Subtractor.circ as structural Verilog: 2 circuits, main circuit main
module main (
  input  A,
  input  B,
  input  Cin,
  output Sum,
  output Cout
);

  wire and_1_out, and_2_out, xor_1_out;

  xor xor_1 (xor_1_out, A, B);
  and and_1 (and_1_out, A, B);
  xor xor_2 (Sum, xor_1_out, Cin);
  and and_2 (and_2_out, Cin, xor_1_out);
  or or_1 (Cout, and_1_out, and_2_out);
endmodule

module Addar_Subtractor (
  input  in_1,
  input  in_2,
  input  in_3,
  input  in_4,
  input  carry_first,
  input  b4,
  input  b3,
  input  b2,
  input  b1,
  input  Control,
  output out_11,
  output out_12,
  output out_13,
  output out_14,
  output out_15
);

  wire main_1_cout, main_2_cout, main_3_cout, main_4_cout, not_1_out, xor_1_out, xor_2_out, xor_3_out,
       xor_4_out;

  xor xor_1 (xor_1_out, Control, b4);
  xor xor_2 (xor_2_out, Control, b3);
  xor xor_3 (xor_3_out, Control, b2);
  xor xor_4 (xor_4_out, Control, b1);
  main main_1 (.A(in_4), .B(xor_4_out), .Cin(carry_first), .Sum(out_14), .Cout(main_1_cout));
  main main_2 (.A(in_3), .B(xor_3_out), .Cin(main_1_cout), .Sum(out_13), .Cout(main_2_cout));
  main main_3 (.A(in_2), .B(xor_2_out), .Cin(main_2_cout), .Sum(out_12), .Cout(main_3_cout));
  main main_4 (.A(in_1), .B(xor_1_out), .Cin(main_3_cout), .Sum(out_11), .Cout(main_4_cout));
  not not_1 (not_1_out, main_4_cout);
  and and_1 (out_15, not_1_out, Control);
endmodule
