// Logisim project Binary to 2421 code converter.circ as structural Verilog: 1 circuit, main circuit main
module main (
  input  A,
  input  B,
  input  C,
  input  D,
  output x,
  output y,
  output z,
  output t
);

  wire and_1_out, and_2_out, and_3_out, and_4_out, not_1_out, not_2_out, not_3_out, or_1_out, or_2_out;

  not not_1 (not_1_out, B);
  not not_2 (not_2_out, C);
  not not_3 (not_3_out, D);
  and and_1 (and_1_out, not_1_out, C);
  and and_2 (and_2_out, not_1_out, not_2_out, D);
  or or_1 (or_1_out, D, C);
  or or_2 (or_2_out, not_3_out, C);
  or or_3 (z, and_1_out, and_2_out, A);
  and and_3 (and_3_out, or_1_out, B);
  and and_4 (and_4_out, or_2_out, B);
  or or_4 (x, and_3_out, A);
  or or_5 (y, and_4_out, A);

  assign t = D;
endmodule
