// Logisim project Custom Priority Encoder.circ as structural Verilog: 1 circuit, main circuit main
module main (
  input  D0,
  input  D1,
  input  D2,
  input  D3,
  output x,
  output y
);

  wire and_1_out, and_2_out, and_3_out, not_1_out, not_2_out, not_3_out, not_4_out, not_5_out, not_6_out,
       not_7_out;

  not not_1 (not_1_out, D1);
  not not_2 (not_2_out, D2);
  not not_3 (not_3_out, D0);
  not not_4 (not_4_out, D2);
  not not_5 (not_5_out, D1);
  not not_6 (not_6_out, D0);
  not not_7 (not_7_out, D2);
  and and_1 (and_1_out, not_3_out, D1, not_4_out);
  and and_2 (and_2_out, D3, not_1_out, not_2_out, not_3_out);
  and and_3 (and_3_out, D3, not_5_out, not_6_out, not_7_out);
  or or_1 (x, D2, and_2_out);
  or or_2 (y, and_1_out, and_3_out);
endmodule
