// Logisim project Ripple carry order.circ as structural Verilog: 2 circuits, main circuit main
module main (
  input  A,
  input  B,
  input  Cin,
  output Sum,
  output Cout
);

  wire and_1_out, and_2_out, xor_1_out;

  xor xor_1 (xor_1_out, A, B);
  and and_1 (and_1_out, A, B);
  xor xor_2 (Sum, xor_1_out, Cin);
  and and_2 (and_2_out, Cin, xor_1_out);
  or or_1 (Cout, and_1_out, and_2_out);
endmodule

module ripple_carry (
  input  in_1,
  input  in_2,
  input  in_3,
  input  in_4,
  input  caray_first,
  input  in_6,
  input  in_7,
  input  in_8,
  input  in_9,
  output out_10,
  output out_11,
  output out_12,
  output out_13,
  output out_14
);

  wire main_1_cout, main_2_cout, main_3_cout;

  main main_1 (.A(in_4), .B(in_9), .Cin(caray_first), .Sum(out_13), .Cout(main_1_cout));
  main main_2 (.A(in_3), .B(in_8), .Cin(main_1_cout), .Sum(out_12), .Cout(main_2_cout));
  main main_3 (.A(in_2), .B(in_7), .Cin(main_2_cout), .Sum(out_11), .Cout(main_3_cout));
  main main_4 (.A(in_1), .B(in_6), .Cin(main_3_cout), .Sum(out_10), .Cout(out_14));
endmodule
